// Logisim project 4-bit-calculator.circ as structural Verilog: 1 circuit, main circuit main
module main (
  input  [3:0] A,
  input  [3:0] B,
  input  SUB,
  output [3:0] RESULT,
  output CARRY_BORROW
);

  wire adder_1_cout;
  wire [3:0] bit_extender_1_out, xor_1_out;

  assign bit_extender_1_out = {{3{SUB}}, SUB};  // Bit_Extender bit_extender_1
  assign xor_1_out = B ^ bit_extender_1_out;  // XOR_Gate xor_1, 4 bits wide
  Adder #(.width(4)) adder_1 (.a(A), .b(xor_1_out), .out(RESULT), .cin(SUB), .cout(adder_1_cout));
  xor xor_2 (CARRY_BORROW, adder_1_cout, SUB);

  // Notes on the sheet:
  //   4-BIT BINARY CALCULATOR
  //   Click input bits with the Poke tool.  SUB: 0 = A + B, 1 = A - B
  //   RESULT = low 4 bits.  Addition: flag = carry.  Subtraction: flag = borrow.
  //   Examples: 0101 + 0011 = 1000; 0101 - 0011 = 0010
endmodule
